// Logisim project counter_logic.circ as structural Verilog: 1 circuit, main circuit main
module main (
);

  wire and_1_out, and_2_out, armed_p2, clock_1_out, nand_1_out, nand_2_out, not_1_out, reset_out, trigger_out;

  Clock clock_1 (.out(clock_1_out));
  Button trigger (.out(trigger_out));
  // Switch armed: pin names not known; wires that end beside it: 1'b1, armed_p2
  Button reset (.out(reset_out));
  Pull_Resistor pull_resistor_1 (.node(armed_p2));
  not not_1 (not_1_out, trigger_out);
  nand nand_1 (nand_1_out, and_1_out, armed_p2);
  nand nand_2 (nand_2_out, not_1_out, nand_1_out);
  and and_1 (and_1_out, nand_2_out, armed_p2);
  and and_2 (and_2_out, clock_1_out, and_1_out);
  Counter counter_1 (.clr(reset_out), .clk(and_2_out));  // open: load, up, count, D, carry, Q
endmodule
